# Fritzing sketch 7 days a week LED (saved by Fritzing 0.9.1b)
breadboards: 1

parts:
  LED1 = LED - 5mm [color="Blue (470nm)" package="5 mm [THT]"]
  R1 = Resistor [tolerance=±5% resistance=220 package=THT]
  Part1 = Intel Edison Arduinobreakout
  LED2 = LED - 5mm [color="Blue (470nm)" package="5 mm [THT]"]
  LED3 = LED - 5mm [color="Blue (470nm)" package="5 mm [THT]"]
  LED4 = LED - 5mm [color="Blue (470nm)" package="5 mm [THT]"]
  LED5 = LED - 5mm [color="Blue (470nm)" package="5 mm [THT]"]
  LED6 = LED - 5mm [color="Blue (470nm)" package="5 mm [THT]"]
  LED7 = LED - 5mm [color="Blue (470nm)" package="5 mm [THT]"]
  R2 = Resistor [tolerance=±5% resistance=220 package=THT]
  R3 = Resistor [tolerance=±5% resistance=220 package=THT]
  R4 = Resistor [tolerance=±5% resistance=220 package=THT]
  R5 = Resistor [tolerance=±5% resistance=220 package=THT]
  R6 = Resistor [tolerance=±5% resistance=220 package=THT]
  R7 = Resistor [tolerance=±5% resistance=220 package=THT]
  R8 = Photocell (LDR) [package=THT]  # not connected

nets:
  N1: LED1.cathode, R1.Pin_1
  N2: LED1.anode, Part1.D2
  N3: R1.Pin_0, Part1.GND, R2.Pin_0, R3.Pin_0, R4.Pin_0, R5.Pin_0, R6.Pin_0, R7.Pin_0
  N4: Part1.D8, LED6.anode
  N5: Part1.D9_PWM, LED7.anode
  N6: Part1.D3_PWM, LED2.anode
  N7: Part1.D4, LED4.anode
  N8: Part1.D5_PWM, LED5.anode
  N9: Part1.D6_PWM, LED3.anode
  N10: LED2.cathode, R2.Pin_1
  N11: LED3.cathode, R5.Pin_1
  N12: LED4.cathode, R3.Pin_1
  N13: LED5.cathode, R4.Pin_1
  N14: LED6.cathode, R6.Pin_1
  N15: LED7.cathode, R7.Pin_1
